// Logisim project memory_blank.circ as structural Verilog
module SR_latch (
  input  R,
  input  S,
  output Q,
  output notQ
);
endmodule

module Gated_SR_latch (
  input  R,
  input  S,
  input  E,
  output Q,
  output notQ
);

  wire undriven, undriven_2;

  SR_latch sr_latch_1 (.R(undriven), .S(undriven_2), .Q(Q), .notQ(notQ));
endmodule

module D_latch (
  input  D,
  input  E,
  output Q,
  output notQ
);

  Gated_SR_latch gated_sr_latch_1 (.E(E), .Q(Q), .notQ(notQ));  // open: R, S
endmodule

module RisingEdge (
  input  CLK,
  output PULSE
);

  wire not_1_out, not_2_out, not_3_out;

  not not_1 (not_1_out, CLK);
  not not_2 (not_2_out, not_1_out);
  not not_3 (not_3_out, not_2_out);
  and and_1 (PULSE, not_3_out, CLK);
endmodule

module FallingEdge (
  input  CLK,
  output PULSE
);

  wire not_1_out;

  not not_1 (not_1_out, CLK);
  RisingEdge risingedge_1 (.CLK(not_1_out), .PULSE(PULSE));
endmodule

module D_flipflop_risingedge (
  input  D,
  input  CLK,
  output Q,
  output notQ
);

  wire undriven;

  D_latch d_latch_1 (.D(D), .E(undriven), .Q(Q), .notQ(notQ));
endmodule

module D_flipflop_masterslave (
  input  D,
  input  CLK,
  output Q,
  output notQ
);

  wire d_latch_1_q, undriven, undriven_2;

  D_latch d_latch_1 (.D(D), .E(undriven), .Q(d_latch_1_q));  // open: notQ
  D_latch d_latch_2 (.D(d_latch_1_q), .E(undriven_2), .Q(Q), .notQ(notQ));
endmodule

module Register4 (
  input  [3:0] D,
  input  CLK,
  output [3:0] Q
);

  wire d_flipflop_masterslave_1_q, d_flipflop_masterslave_2_q, d_flipflop_masterslave_3_q,
       d_flipflop_masterslave_4_q, undriven, undriven_2, undriven_3, undriven_4;

  D_flipflop_masterslave d_flipflop_masterslave_1 (
    .D(undriven), .CLK(CLK), .Q(d_flipflop_masterslave_1_q));  // open: notQ
  D_flipflop_masterslave d_flipflop_masterslave_2 (
    .D(undriven_2), .CLK(CLK), .Q(d_flipflop_masterslave_2_q));  // open: notQ
  D_flipflop_masterslave d_flipflop_masterslave_3 (
    .D(undriven_3), .CLK(CLK), .Q(d_flipflop_masterslave_3_q));  // open: notQ
  D_flipflop_masterslave d_flipflop_masterslave_4 (
    .D(undriven_4), .CLK(CLK), .Q(d_flipflop_masterslave_4_q));  // open: notQ
endmodule

module Register16 (
  input  [15:0] D,
  input  CLK,
  output [15:0] Q
);

  wire [3:0] register4_1_q, register4_2_q, register4_3_q, register4_4_q, undriven, undriven_2, undriven_3,
       undriven_4;

  Register4 register4_1 (.D(undriven), .CLK(CLK), .Q(register4_1_q));
  Register4 register4_2 (.D(undriven_2), .CLK(CLK), .Q(register4_2_q));
  Register4 register4_3 (.D(undriven_3), .CLK(CLK), .Q(register4_3_q));
  Register4 register4_4 (.D(undriven_4), .CLK(CLK), .Q(register4_4_q));
endmodule

module Register_WE_Bad (
  input  [15:0] D,
  input  CLK,
  input  WE,
  output [15:0] Q
);

  wire and_1_out;

  and and_1 (and_1_out, CLK, WE);
  Register16 register16_1 (.D(D), .CLK(and_1_out), .Q(Q));

  // Notes on the sheet:
  //   Gated clock is bad!
endmodule

module Register_WE (
  input  [15:0] D,
  input  CLK,
  input  WE,
  output [15:0] Q
);

  Register16 register16_1 (.CLK(CLK), .Q(Q));  // open: D
endmodule

module ShiftRegister (
  input  D_IN,
  input  CLK,
  input  WE,
  output [4:0] PAR_OUT,
  output D_OUT
);

  Register #(.width(1)) register_1 (.D(D_IN), .en(WE), .clk(CLK), .Q(PAR_OUT[0]));  // open: clr
  Register #(.width(1)) register_2 (.D(PAR_OUT[0]), .en(WE), .clk(CLK), .Q(PAR_OUT[1]));  // open: clr
  Register #(.width(1)) register_3 (.D(PAR_OUT[1]), .en(WE), .clk(CLK), .Q(PAR_OUT[2]));  // open: clr
  Register #(.width(1)) register_4 (.D(PAR_OUT[2]), .en(WE), .clk(CLK), .Q(PAR_OUT[3]));  // open: clr
  Register #(.width(1)) register_5 (.D(PAR_OUT[3]), .en(WE), .clk(CLK), .Q(D_OUT));  // open: clr

  assign PAR_OUT[4] = D_OUT;
endmodule

module ShiftRegister8 (
  input  [7:0] D_IN,
  input  CLK,
  input  WE,
  output [39:0] PAR_OUT,
  output [7:0] D_OUT
);

  Register register_1 (.D(D_IN), .en(WE), .clk(CLK), .Q(PAR_OUT[7:0]));  // open: clr
  Register register_2 (.D(PAR_OUT[7:0]), .en(WE), .clk(CLK), .Q(PAR_OUT[15:8]));  // open: clr
  Register register_3 (.D(PAR_OUT[15:8]), .en(WE), .clk(CLK), .Q(PAR_OUT[23:16]));  // open: clr
  Register register_4 (.D(PAR_OUT[23:16]), .en(WE), .clk(CLK), .Q(PAR_OUT[31:24]));  // open: clr
  Register register_5 (.D(PAR_OUT[31:24]), .en(WE), .clk(CLK), .Q(D_OUT));  // open: clr

  assign PAR_OUT[39:32] = D_OUT;
endmodule

module Memory16x4 (
  input  [15:0] D_IN,
  input  CLK,
  input  WE,
  input  [1:0] ADDR,
  output [15:0] D_OUT
);

  wire undriven, undriven_2, undriven_3, undriven_4;
  wire [15:0] register_1_q, register_2_q, register_3_q, register_4_q;

  Register #(.width(16)) register_1 (.D(D_IN), .en(undriven_4), .clk(CLK), .Q(register_1_q));  // open: clr
  Register #(.width(16)) register_2 (.D(D_IN), .en(undriven), .clk(CLK), .Q(register_2_q));  // open: clr
  Register #(.width(16)) register_3 (.D(D_IN), .en(undriven_2), .clk(CLK), .Q(register_3_q));  // open: clr
  Register #(.width(16)) register_4 (.D(D_IN), .en(undriven_3), .clk(CLK), .Q(register_4_q));  // open: clr
endmodule

module Memory16x16 (
  input  [15:0] D_IN,
  input  CLK,
  input  WE,
  input  [3:0] ADDR,
  output [15:0] D_OUT
);

  wire undriven, undriven_2, undriven_3, undriven_4;
  wire [1:0] undriven_5;
  wire [15:0] memory16x4_1_d_out, memory16x4_2_d_out, memory16x4_3_d_out, memory16x4_4_d_out;

  Memory16x4 memory16x4_1 (.D_IN(D_IN), .CLK(CLK), .WE(undriven_4), .ADDR(undriven_5), .D_OUT(memory16x4_1_d_out));
  Memory16x4 memory16x4_2 (.D_IN(D_IN), .CLK(CLK), .WE(undriven), .ADDR(undriven_5), .D_OUT(memory16x4_2_d_out));
  Memory16x4 memory16x4_3 (.D_IN(D_IN), .CLK(CLK), .WE(undriven_2), .ADDR(undriven_5), .D_OUT(memory16x4_3_d_out));
  Memory16x4 memory16x4_4 (.D_IN(D_IN), .CLK(CLK), .WE(undriven_3), .ADDR(undriven_5), .D_OUT(memory16x4_4_d_out));
endmodule

module T_flipflop (
  input  T,
  input  CLK,
  output Q
);

  wire undriven;

  Register #(.width(1)) register_1 (.D(undriven), .en(T), .clk(CLK), .Q(Q));  // open: clr
endmodule

module T_flipflop_osc (
);

  wire button_1_out, clock_1_out, digital_oscilloscope_1_p3, t_ff_1_q;

  Clock clock_1 (.out(clock_1_out));
  T_Flip_Flop t_ff_1 (.T(1'b1), .clk(clock_1_out), .Q(t_ff_1_q), .reset(button_1_out));  // open: Qn, preset
  Button button_1 (.out(button_1_out));
  // Digital_Oscilloscope digital_oscilloscope_1: pin names not known; wires that end beside it: clock_1_out, t_ff_1_q, digital_oscilloscope_1_p3
  Button button_2 (.out(digital_oscilloscope_1_p3));
endmodule

module T_flipflop_osc2 (
);

  wire button_1_out, clock_1_out, digital_oscilloscope_1_p4, digital_oscilloscope_1_p5, t_ff_1_q, t_ff_2_q;

  Clock clock_1 (.out(clock_1_out));
  T_Flip_Flop t_ff_1 (.T(1'b1), .clk(clock_1_out), .Q(t_ff_1_q), .reset(button_1_out));  // open: Qn, preset
  Button button_1 (.out(button_1_out));
  T_Flip_Flop t_ff_2 (.T(1'b1), .clk(t_ff_1_q), .Q(t_ff_2_q), .reset(button_1_out));  // open: Qn, preset
  // Digital_Oscilloscope digital_oscilloscope_1: pin names not known; wires that end beside it: clock_1_out, t_ff_1_q, t_ff_2_q, digital_oscilloscope_1_p4, digital_oscilloscope_1_p5
  T_Flip_Flop t_ff_3 (
    .T(1'b1), .clk(t_ff_2_q), .Q(digital_oscilloscope_1_p4), .reset(button_1_out));  // open: Qn, preset
  Button button_2 (.out(digital_oscilloscope_1_p5));
endmodule
